# Fritzing sketch Nano_AMS-1 (saved by Fritzing 0.9.3b)
breadboards: 1

parts:
  Part2 = Arduino Nano (Rev3.0)
  RHT2 = Humidity and Temperature Sensor RHT03 [part_number=DHT22]

nets:
  N1: Part2.D0/RX, Part2.D8, Part2.D9, Part2.D10, RHT2.Data-signal
  N2: Part2.RESET, Part2.GND, Part2.D2, RHT2.GND_2
  3V3: Part2.AREF, Part2.3V3, Part2.D13/SCK, RHT2.Vcc

notes:
  DHT22
  Arduino Nano
